// Logisim project stage2.circ as structural Verilog: 1 circuit, main circuit main
module main (
  input  in_1,
  input  in_2,
  input  in_3,
  input  in_4
);

  wire and_1_out, and_2_out, and_3_out, and_4_out, and_5_out, button_1_out, clock_1_out, d_ff_1_q, d_ff_1_qn,
       j_k_ff_4_qn, or_1_out;
  wire [3:0] j_k_ff_1_q;

  Hex_Digit_Display hex_digit_display_1 ();  // open: value, dp
  Hex_Digit_Display hex_digit_display_2 ();  // open: value, dp
  Button button_1 (.out(button_1_out));
  Hex_Digit_Display hex_digit_display_3 (.value({in_3, in_4, in_2, in_1}));  // open: dp
  Hex_Digit_Display hex_digit_display_4 (.value(j_k_ff_1_q));  // open: dp
  Button button_2 ();  // open: out
  Button button_3 ();  // open: out
  Hex_Digit_Display hex_digit_display_5 ();  // open: value, dp
  Hex_Digit_Display hex_digit_display_6 ();  // open: value, dp
  Hex_Digit_Display hex_digit_display_7 ();  // open: value, dp
  LED led_1 (.in(d_ff_1_q));
  Hex_Digit_Display hex_digit_display_8 ();  // open: value, dp
  D_Flip_Flop d_ff_1 (.D(d_ff_1_qn), .clk(button_1_out), .Q(d_ff_1_q), .Qn(d_ff_1_qn));  // open: preset, reset
  Clock clock_1 (.out(clock_1_out));
  and and_1 (and_1_out, d_ff_1_q, clock_1_out);
  J_K_Flip_Flop j_k_ff_1 (.J(d_ff_1_q), .K(d_ff_1_q), .clk(and_1_out), .Q(j_k_ff_1_q[0]));  // open: Qn, preset, reset
  and and_2 (and_2_out, j_k_ff_1_q[0], j_k_ff_4_qn);
  J_K_Flip_Flop j_k_ff_2 (.J(and_2_out), .K(and_2_out), .clk(and_1_out), .Q(j_k_ff_1_q[1]));  // open: Qn, preset, reset
  and and_3 (and_3_out, j_k_ff_1_q[0], j_k_ff_1_q[1]);
  J_K_Flip_Flop j_k_ff_3 (.J(and_3_out), .K(and_3_out), .clk(and_1_out), .Q(j_k_ff_1_q[2]));  // open: Qn, preset, reset
  and and_4 (and_4_out, j_k_ff_1_q[3], j_k_ff_1_q[0]);
  and and_5 (and_5_out, and_3_out, j_k_ff_1_q[2]);
  or or_1 (or_1_out, and_4_out, and_5_out);
  J_K_Flip_Flop j_k_ff_4 (
    .J(or_1_out), .K(or_1_out), .clk(and_1_out), .Q(j_k_ff_1_q[3]), .Qn(j_k_ff_4_qn));  // open: preset, reset

  // Notes on the sheet:
  //   Elapsed Time
  //   Minutes
  //   :
  //   Start / Stop
  //   Seconds
  //   Stopwatch Interface
  //   Split
  //   Reset
  //   Minutes
  //   Clock Started
  //   Split Time
  //   :
  //   Seconds
  //   Stage 1
  //   Stage 2
endmodule
