// Logisim project stage3.circ as structural Verilog: 1 circuit, main circuit main
module main (
  input  in_1
);

  wire and_1_out, and_2_out, and_3_out, and_4_out, and_5_out, and_6_out, and_7_out, and_8_out, and_9_out,
       button_1_out, button_3_out, clock_1_out, d_ff_1_q, d_ff_1_qn, j_k_ff_6_qn, j_k_ff_7_qn, not_1_out,
       or_1_out, or_2_out;
  wire [2:0] j_k_ff_2_q;
  wire [3:0] j_k_ff_1_q;

  Hex_Digit_Display hex_digit_display_1 ();  // open: value, dp
  Hex_Digit_Display hex_digit_display_2 ();  // open: value, dp
  Button button_1 (.out(button_1_out));
  Hex_Digit_Display hex_digit_display_3 (.value({in_1, j_k_ff_2_q}));  // open: dp
  Hex_Digit_Display hex_digit_display_4 (.value(j_k_ff_1_q));  // open: dp
  Button button_2 ();  // open: out
  Button button_3 (.out(button_3_out));
  Hex_Digit_Display hex_digit_display_5 ();  // open: value, dp
  Hex_Digit_Display hex_digit_display_6 ();  // open: value, dp
  Hex_Digit_Display hex_digit_display_7 ();  // open: value, dp
  LED led_1 (.in(d_ff_1_q));
  Hex_Digit_Display hex_digit_display_8 ();  // open: value, dp
  D_Flip_Flop d_ff_1 (
    .D(d_ff_1_qn), .clk(button_1_out), .Q(d_ff_1_q), .Qn(d_ff_1_qn), .reset(button_3_out));  // open: preset
  Clock clock_1 (.out(clock_1_out));
  and and_1 (and_1_out, d_ff_1_q, clock_1_out);
  J_K_Flip_Flop j_k_ff_1 (
    .J(d_ff_1_q), .K(d_ff_1_q), .clk(and_1_out), .Q(j_k_ff_1_q[0]), .reset(button_3_out));  // open: Qn, preset
  and and_2 (and_2_out, j_k_ff_1_q[0], j_k_ff_1_q[3]);
  not not_1 (not_1_out, and_2_out);
  and and_3 (and_3_out, j_k_ff_1_q[0], j_k_ff_6_qn);
  J_K_Flip_Flop j_k_ff_2 (
    .J(not_1_out), .K(not_1_out), .clk(not_1_out), .Q(j_k_ff_2_q[0]), .reset(button_3_out));  // open: Qn, preset
  J_K_Flip_Flop j_k_ff_3 (
    .J(and_3_out), .K(and_3_out), .clk(and_1_out), .Q(j_k_ff_1_q[1]), .reset(button_3_out));  // open: Qn, preset
  and and_4 (and_4_out, j_k_ff_1_q[0], j_k_ff_1_q[1]);
  and and_5 (and_5_out, j_k_ff_2_q[0], j_k_ff_7_qn);
  J_K_Flip_Flop j_k_ff_4 (
    .J(and_4_out), .K(and_4_out), .clk(and_1_out), .Q(j_k_ff_1_q[2]), .reset(button_3_out));  // open: Qn, preset
  J_K_Flip_Flop j_k_ff_5 (
    .J(and_5_out), .K(and_5_out), .clk(not_1_out), .Q(j_k_ff_2_q[1]), .reset(button_3_out));  // open: Qn, preset
  and and_6 (and_6_out, j_k_ff_1_q[3], j_k_ff_1_q[0]);
  and and_7 (and_7_out, and_4_out, j_k_ff_1_q[2]);
  and and_8 (and_8_out, j_k_ff_2_q[2], j_k_ff_2_q[0]);
  and and_9 (and_9_out, and_5_out, j_k_ff_2_q[1]);
  or or_1 (or_1_out, and_6_out, and_7_out);
  or or_2 (or_2_out, and_8_out, and_9_out);
  J_K_Flip_Flop j_k_ff_6 (
    .J(or_1_out), .K(or_1_out), .clk(and_1_out), .Q(j_k_ff_1_q[3]), .Qn(j_k_ff_6_qn), .reset(button_3_out));  // open: preset
  J_K_Flip_Flop j_k_ff_7 (
    .J(or_2_out), .K(or_2_out), .clk(not_1_out), .Q(j_k_ff_2_q[2]), .Qn(j_k_ff_7_qn), .reset(button_3_out));  // open: preset

  // Notes on the sheet:
  //   Elapsed Time
  //   Minutes
  //   :
  //   Start / Stop
  //   Seconds
  //   Stopwatch Interface
  //   Split
  //   Reset
  //   Minutes
  //   Clock Started
  //   Split Time
  //   :
  //   Seconds
  //   Stage 1
  //   Stage 2
  //   Stage 3
endmodule
