// Logisim project stage5.circ as structural Verilog: 1 circuit, main circuit main
module main (
  input  in_1,
  input  in_2
);

  wire and_1_out, and_2_out, and_3_out, and_4_out, and_5_out, and_6_out, and_7_out, and_8_out, and_9_out,
       and_10_out, and_11_out, and_12_out, and_13_out, and_14_out, and_15_out, and_16_out, and_17_out,
       and_18_out, and_19_out, and_20_out, button_1_out, button_2_out, button_3_out, clock_1_out, d_ff_1_q,
       d_ff_1_qn, j_k_ff_12_qn, j_k_ff_13_qn, j_k_ff_14_qn, j_k_ff_15_qn, not_1_out, not_2_out, not_3_out,
       or_1_out, or_2_out, or_3_out, or_4_out;
  wire [2:0] d_ff_3_q, j_k_ff_4_q;
  wire [3:0] d_ff_2_q, d_ff_4_q, d_ff_5_q, j_k_ff_1_q, j_k_ff_2_q, j_k_ff_6_q;

  Hex_Digit_Display hex_digit_display_1 (.value(j_k_ff_6_q));  // open: dp
  Hex_Digit_Display hex_digit_display_2 (.value(j_k_ff_2_q));  // open: dp
  Button button_1 (.out(button_1_out));
  Hex_Digit_Display hex_digit_display_3 (.value({in_1, j_k_ff_4_q}));  // open: dp
  Hex_Digit_Display hex_digit_display_4 (.value(j_k_ff_1_q));  // open: dp
  Button button_2 (.out(button_2_out));
  Button button_3 (.out(button_3_out));
  Hex_Digit_Display hex_digit_display_5 (.value(d_ff_5_q));  // open: dp
  Hex_Digit_Display hex_digit_display_6 (.value(d_ff_4_q));  // open: dp
  Hex_Digit_Display hex_digit_display_7 (.value({in_2, d_ff_3_q}));  // open: dp
  LED led_1 (.in(d_ff_1_q));
  Hex_Digit_Display hex_digit_display_8 (.value(d_ff_2_q));  // open: dp
  D_Flip_Flop d_ff_1 (
    .D(d_ff_1_qn), .clk(button_1_out), .Q(d_ff_1_q), .Qn(d_ff_1_qn), .reset(button_3_out));  // open: preset
  Clock clock_1 (.out(clock_1_out));
  and and_1 (and_1_out, d_ff_1_q, clock_1_out);
  J_K_Flip_Flop j_k_ff_1 (
    .J(d_ff_1_q), .K(d_ff_1_q), .clk(and_1_out), .Q(j_k_ff_1_q[0]), .reset(button_3_out));  // open: Qn, preset
  J_K_Flip_Flop j_k_ff_2 (
    .J(not_3_out), .K(not_3_out), .clk(not_3_out), .Q(j_k_ff_2_q[0]), .reset(button_3_out));  // open: Qn, preset
  and and_2 (and_2_out, j_k_ff_1_q[0], j_k_ff_1_q[3]);
  not not_1 (not_1_out, and_2_out);
  and and_3 (and_3_out, j_k_ff_2_q[0], j_k_ff_2_q[3]);
  not not_2 (not_2_out, and_3_out);
  and and_4 (and_4_out, j_k_ff_1_q[0], j_k_ff_12_qn);
  and and_5 (and_5_out, j_k_ff_2_q[0], j_k_ff_14_qn);
  J_K_Flip_Flop j_k_ff_3 (
    .J(and_4_out), .K(and_4_out), .clk(and_1_out), .Q(j_k_ff_1_q[1]), .reset(button_3_out));  // open: Qn, preset
  J_K_Flip_Flop j_k_ff_4 (
    .J(not_1_out), .K(not_1_out), .clk(not_1_out), .Q(j_k_ff_4_q[0]), .reset(button_3_out));  // open: Qn, preset
  J_K_Flip_Flop j_k_ff_5 (
    .J(and_5_out), .K(and_5_out), .clk(not_3_out), .Q(j_k_ff_2_q[1]), .reset(button_3_out));  // open: Qn, preset
  J_K_Flip_Flop j_k_ff_6 (
    .J(not_2_out), .K(not_2_out), .clk(not_2_out), .Q(j_k_ff_6_q[0]), .reset(button_3_out));  // open: Qn, preset
  and and_6 (and_6_out, j_k_ff_1_q[0], j_k_ff_1_q[1]);
  and and_7 (and_7_out, j_k_ff_4_q[0], j_k_ff_13_qn);
  and and_8 (and_8_out, j_k_ff_2_q[0], j_k_ff_2_q[1]);
  J_K_Flip_Flop j_k_ff_7 (
    .J(and_6_out), .K(and_6_out), .clk(and_1_out), .Q(j_k_ff_1_q[2]), .reset(button_3_out));  // open: Qn, preset
  J_K_Flip_Flop j_k_ff_8 (
    .J(and_7_out), .K(and_7_out), .clk(not_1_out), .Q(j_k_ff_4_q[1]), .reset(button_3_out));  // open: Qn, preset
  J_K_Flip_Flop j_k_ff_9 (
    .J(and_8_out), .K(and_8_out), .clk(not_3_out), .Q(j_k_ff_2_q[2]), .reset(button_3_out));  // open: Qn, preset
  J_K_Flip_Flop j_k_ff_10 (
    .J(and_9_out), .K(and_9_out), .clk(not_2_out), .Q(j_k_ff_6_q[1]), .reset(button_3_out));  // open: Qn, preset
  and and_9 (and_9_out, j_k_ff_6_q[0], j_k_ff_15_qn);
  and and_10 (and_10_out, j_k_ff_1_q[3], j_k_ff_1_q[0]);
  and and_11 (and_11_out, and_6_out, j_k_ff_1_q[2]);
  and and_12 (and_12_out, j_k_ff_4_q[2], j_k_ff_4_q[0]);
  and and_13 (and_13_out, and_7_out, j_k_ff_4_q[1]);
  and and_14 (and_14_out, j_k_ff_2_q[3], j_k_ff_2_q[0]);
  and and_15 (and_15_out, and_8_out, j_k_ff_2_q[2]);
  and and_16 (and_16_out, j_k_ff_6_q[0], j_k_ff_6_q[1]);
  or or_1 (or_1_out, and_10_out, and_11_out);
  or or_2 (or_2_out, and_12_out, and_13_out);
  or or_3 (or_3_out, and_14_out, and_15_out);
  J_K_Flip_Flop j_k_ff_11 (
    .J(and_16_out), .K(and_16_out), .clk(not_2_out), .Q(j_k_ff_6_q[2]), .reset(button_3_out));  // open: Qn, preset
  J_K_Flip_Flop j_k_ff_12 (
    .J(or_1_out), .K(or_1_out), .clk(and_1_out), .Q(j_k_ff_1_q[3]), .Qn(j_k_ff_12_qn), .reset(button_3_out));  // open: preset
  J_K_Flip_Flop j_k_ff_13 (
    .J(or_2_out), .K(or_2_out), .clk(not_1_out), .Q(j_k_ff_4_q[2]), .Qn(j_k_ff_13_qn), .reset(button_3_out));  // open: preset
  J_K_Flip_Flop j_k_ff_14 (
    .J(or_3_out), .K(or_3_out), .clk(not_3_out), .Q(j_k_ff_2_q[3]), .Qn(j_k_ff_14_qn), .reset(button_3_out));  // open: preset
  and and_17 (and_17_out, j_k_ff_6_q[3], j_k_ff_6_q[0]);
  and and_18 (and_18_out, and_16_out, j_k_ff_6_q[2]);
  or or_4 (or_4_out, and_17_out, and_18_out);
  and and_19 (and_19_out, j_k_ff_4_q[0], j_k_ff_4_q[2]);
  J_K_Flip_Flop j_k_ff_15 (
    .J(or_4_out), .K(or_4_out), .clk(not_2_out), .Q(j_k_ff_6_q[3]), .Qn(j_k_ff_15_qn), .reset(button_3_out));  // open: preset
  not not_3 (not_3_out, and_19_out);
  and and_20 (and_20_out, button_2_out, d_ff_1_q);
  D_Flip_Flop d_ff_2 (.D(j_k_ff_1_q[0]), .clk(and_20_out), .Q(d_ff_2_q[0]), .reset(button_3_out));  // open: Qn, preset
  D_Flip_Flop d_ff_3 (.D(j_k_ff_4_q[0]), .clk(and_20_out), .Q(d_ff_3_q[0]), .reset(button_3_out));  // open: Qn, preset
  D_Flip_Flop d_ff_4 (.D(j_k_ff_2_q[0]), .clk(and_20_out), .Q(d_ff_4_q[0]), .reset(button_3_out));  // open: Qn, preset
  D_Flip_Flop d_ff_5 (.D(j_k_ff_6_q[0]), .clk(and_20_out), .Q(d_ff_5_q[0]), .reset(button_3_out));  // open: Qn, preset
  D_Flip_Flop d_ff_6 (.D(j_k_ff_1_q[1]), .clk(and_20_out), .Q(d_ff_2_q[1]), .reset(button_3_out));  // open: Qn, preset
  D_Flip_Flop d_ff_7 (.D(j_k_ff_4_q[1]), .clk(and_20_out), .Q(d_ff_3_q[1]), .reset(button_3_out));  // open: Qn, preset
  D_Flip_Flop d_ff_8 (.D(j_k_ff_2_q[1]), .clk(and_20_out), .Q(d_ff_4_q[1]), .reset(button_3_out));  // open: Qn, preset
  D_Flip_Flop d_ff_9 (.D(j_k_ff_6_q[1]), .clk(and_20_out), .Q(d_ff_5_q[1]), .reset(button_3_out));  // open: Qn, preset
  D_Flip_Flop d_ff_10 (.D(j_k_ff_1_q[2]), .clk(and_20_out), .Q(d_ff_2_q[2]), .reset(button_3_out));  // open: Qn, preset
  D_Flip_Flop d_ff_11 (.D(j_k_ff_4_q[2]), .clk(and_20_out), .Q(d_ff_3_q[2]), .reset(button_3_out));  // open: Qn, preset
  D_Flip_Flop d_ff_12 (.D(j_k_ff_2_q[2]), .clk(and_20_out), .Q(d_ff_4_q[2]), .reset(button_3_out));  // open: Qn, preset
  D_Flip_Flop d_ff_13 (.D(j_k_ff_6_q[2]), .clk(and_20_out), .Q(d_ff_5_q[2]), .reset(button_3_out));  // open: Qn, preset
  D_Flip_Flop d_ff_14 (.D(j_k_ff_1_q[3]), .clk(and_20_out), .Q(d_ff_2_q[3]), .reset(button_3_out));  // open: Qn, preset
  D_Flip_Flop d_ff_15 (.D(j_k_ff_2_q[3]), .clk(and_20_out), .Q(d_ff_4_q[3]), .reset(button_3_out));  // open: Qn, preset
  D_Flip_Flop d_ff_16 (.D(j_k_ff_6_q[3]), .clk(and_20_out), .Q(d_ff_5_q[3]), .reset(button_3_out));  // open: Qn, preset

  // Notes on the sheet:
  //   Elapsed Time
  //   Minutes
  //   :
  //   Start / Stop
  //   Seconds
  //   Stopwatch Interface
  //   Split
  //   Reset
  //   Minutes
  //   Clock Started
  //   Split Time
  //   :
  //   Seconds
  //   Stage 1
  //   Stage 2
  //   Stage 3
  //   Stage 4
  //   Stage 5
endmodule
